// Logisim project 2 4译码器.circ as structural Verilog: 1 circuit, main circuit main
module main (
  input  in_1,
  input  A1,
  input  A2,
  output out_4,
  output out_5,
  output out_6,
  output out_7
);

  wire not_1_out, not_2_out;

  not not_1 (not_1_out, A2);
  not not_2 (not_2_out, A1);
  and and_1 (out_4, in_1, not_2_out, not_1_out);
  and and_2 (out_5, in_1, not_2_out, A2);
  and and_3 (out_6, in_1, A1, not_1_out);
  and and_4 (out_7, in_1, A1, A2);

  // Notes on the sheet:
  //   E
endmodule
