// Logisim project jicunzu.circ as structural Verilog: 1 circuit, main circuit main
module main (
  input  in_1,
  input  D,
  input  in_3,
  input  D_2,
  output Q,
  output minus_Q,
  output minus_Q_2,
  output out_8,
  output minus_Q_3
);

  wire and_1_out, and_2_out, and_3_out, and_4_out, and_5_out, and_6_out, and_7_out, and_8_out, nor_2_out,
       nor_3_out, nor_4_out, not_1_out, not_2_out, not_3_out, not_4_out, not_5_out, not_6_out;

  not not_1 (not_1_out, in_1);
  not not_2 (not_2_out, in_3);
  not not_3 (not_3_out, D);
  not not_4 (not_4_out, nor_3_out);
  not not_5 (not_5_out, D_2);
  not not_6 (not_6_out, nor_2_out);
  and and_1 (and_1_out, not_1_out, not_3_out);
  and and_2 (and_2_out, not_1_out, D);
  and and_3 (and_3_out, in_1, not_4_out);
  and and_4 (and_4_out, in_1, nor_3_out);
  and and_5 (and_5_out, not_2_out, not_5_out);
  and and_6 (and_6_out, not_2_out, D_2);
  and and_7 (and_7_out, in_3, not_6_out);
  and and_8 (and_8_out, in_3, nor_2_out);
  nor nor_1 (minus_Q_2, nor_2_out, and_6_out);
  nor nor_2 (nor_2_out, and_5_out, minus_Q_2);
  nor nor_3 (nor_3_out, and_1_out, nor_4_out);
  nor nor_4 (nor_4_out, nor_3_out, and_2_out);
  nor nor_5 (Q, and_3_out, minus_Q);
  nor nor_6 (minus_Q, Q, and_4_out);
  nor nor_7 (out_8, and_7_out, minus_Q_3);
  nor nor_8 (minus_Q_3, out_8, and_8_out);

  // Notes on the sheet:
  //   CLK
  //   CLK
  //   CLK
  //   CLK
  //   D
  //   CLK
  //   D
  //   -D
  //   -D
  //   -D
  //   -D
  //   R
  //   S
  //   R
  //   S
  //   R
  //   S
  //   R
  //   S
  //   Q
  //   -Q
  //   Q
  //   Q
  //   主
  //   从
endmodule
